# Fritzing sketch auto-plant-watering-board-mkr1000 (saved by Fritzing 0.9.3b)
circuit board: 9.69166cm x 4.75644cm
stripboards: 1

parts:
  U1 = Voltage Regulator - 5V [package="TO220 [THT]"]
  J2 = Screw terminal - 2 pins [package=THT]
  J4 = Screw terminal - 2 pins [package=THT]
  LED2 = LED - 5mm [color="Red (633nm)" package="5 mm [THT]"]
  J3 = JST-B3P-VH [part_number=JST-B3P-VH package=THT]
  R3 = Resistor [tolerance=±5% resistance=150 package="1206 [SMD]"]
  R2 = Resistor [tolerance=±10% resistance=150 package="1206 [SMD]"]
  D1 = Rectifier Diode [part_number=1N4001 package="300 mil [THT]"]
  Q2 = Basic FET N-Channel [package="TO220 [THT]"]
  Part2 = Arduino MKR1000

nets:
  N1: U1.input_voltage, J2.pin1, J4.pin2, D1.cathode
  N2: U1.GND, J2.pin2
  N3: U1.output_voltage, LED2.cathode, J3.pin3, Q2.source, Part2.GND
  N4: J4.pin1, D1.anode, Q2.drain
  N5: LED2.anode, R3.Pin_1
  N6: J3.pin2, Part2.VCC
  N7: J3.pin1, Part2.A1
  N8: R3.Pin_0, Part2.D11_SDA
  N9: R2.Pin_0, Q2.gate
  N10: R2.Pin_1, Part2.D8_MOSI

notes:
  Arduino MKR 1000
  Analog Sensor Pump Control
  WAM 2020

custom parts:
  Arduino MKR1000: MKR1000 is a powerful board that combines the functionality of the Zero and the Wi-Fi Shield. It is the ideal solution for makers wanting to design IoT projects with minimal previous experience in networking
